// Logisim project lab003.circ as structural Verilog: 5 circuits, main circuit ex002
module ex001 (
  input  in_1,
  output out_2
);

  nand nand_1 (out_2, in_1, in_1);

  // Notes on the sheet:
  //   NOT
endmodule

module ex002 (
  input  in_1,
  input  in_2,
  output out_3
);

  wire nand_1_out;

  nand nand_1 (nand_1_out, in_1, in_2);
  not not_1 (out_3, nand_1_out);

  // Notes on the sheet:
  //   AND
endmodule

module ex003 (
  input  in_1,
  input  in_2,
  output out_3
);

  wire nand_1_out, nand_2_out;

  nand nand_1 (nand_1_out, in_1, in_1);
  nand nand_2 (nand_2_out, in_2, in_2);
  nand nand_3 (out_3, nand_1_out, nand_2_out);

  // Notes on the sheet:
  //   OR
endmodule

module ex004 (
  input  in_1,
  input  in_2,
  output out_3
);

  wire p1_out, p2_out, p3_out;

  nand p1 (p1_out, in_1, in_2);
  nand p2 (p2_out, in_1, p1_out);
  nand p3 (p3_out, p1_out, in_2);
  nand pF (out_3, p2_out, p3_out);

  // Notes on the sheet:
  //   EXCLUSIVE OR
endmodule

module ex005 (
);


  // Notes on the sheet:
  //   dá pra construir as portas báscias apenas com NAO-E, logo, é possível construir qualquer sistema apenas com NAO-E
endmodule
