// Logisim project lab05.circ as structural Verilog: 2 circuits, main circuit main
module main (
  input  d3,
  input  d2,
  input  d1,
  input  d0
);

  wire equacoes_a, equacoes_b, equacoes_c, equacoes_d, equacoes_e, equacoes_f, equacoes_g;

  equacoes equacoes (
    .d3(d3), .d2(d2), .d1(d1), .d0(d0), .a(equacoes_a), .b(equacoes_b), .c(equacoes_c), .d(equacoes_d),
    .e(equacoes_e), .f(equacoes_f), .g(equacoes_g));
  _7_Segment_Display u_7_segment_display_1 (
    .g(equacoes_g), .f(equacoes_f), .a(equacoes_a), .b(equacoes_b), .e(equacoes_e), .d(equacoes_d),
    .c(equacoes_c));  // open: dp

  // Notes on the sheet:
  //   B
  //   A
  //   C
  //   D
endmodule

module equacoes (
  input  d3,
  input  d2,
  input  d1,
  input  d0,
  output a,
  output b,
  output c,
  output d,
  output e,
  output f,
  output g
);

  wire and_1_out, and_2_out, and_3_out, and_4_out, and_5_out, and_6_out, and_7_out, and_8_out, and_9_out,
       and_10_out, and_11_out, and_12_out, and_13_out, and_14_out, and_15_out, and_16_out, and_17_out,
       and_18_out, and_19_out, and_20_out, and_21_out, and_22_out, and_23_out, ok_2_out, ok_3_out, ok_out;

  and and_1 (and_1_out, ~d3, ~d2, ~d0);  // AND_Gate
  and and_2 (and_2_out, ~d3, d2, d0);  // AND_Gate
  and and_3 (and_3_out, ~d3, d1);  // AND_Gate
  and and_4 (and_4_out, d3, ~d2, ~d1);  // AND_Gate
  and and_5 (and_5_out, ~d3, ~d1, ~d0);  // AND_Gate
  and and_6 (and_6_out, ~d3, ~d2);  // AND_Gate
  and and_7 (and_7_out, ~d3, d1, d0);  // AND_Gate
  and and_8 (and_8_out, ~d2, ~d1);  // AND_Gate
  and and_9 (and_9_out, ~d3, d2);  // AND_Gate
  and and_10 (and_10_out, ~d3, d0);  // AND_Gate
  and and_11 (and_11_out, ~d2, ~d1);  // AND_Gate
  and ok (ok_out, d3, ~d2, ~d1);  // AND_Gate
  and ok_2 (ok_2_out, ~d3, ~d2, d1);  // AND_Gate
  and and_12 (and_12_out, ~d3, d1, ~d0);  // AND_Gate
  and and_13 (and_13_out, ~d3, ~d2, ~d0);  // AND_Gate
  and ok_3 (ok_3_out, ~d3, d2, ~d1, d0);  // AND_Gate
  and and_14 (and_14_out, ~d2, ~d1, ~d0);  // AND_Gate
  and and_15 (and_15_out, ~d3, d1, ~d0);  // AND_Gate
  and and_16 (and_16_out, d3, ~d2, ~d1);  // AND_Gate
  and and_17 (and_17_out, ~d3, ~d1, ~d0);  // AND_Gate
  and and_18 (and_18_out, ~d3, d2, d1);  // AND_Gate
  and and_19 (and_19_out, ~d3, d2, d0);  // AND_Gate
  and and_20 (and_20_out, ~d3, d2, ~d0);  // AND_Gate
  and and_21 (and_21_out, ~d3, d2, ~d1);  // AND_Gate
  and and_22 (and_22_out, ~d3, ~d2, d1);  // AND_Gate
  and and_23 (and_23_out, d3, ~d2, ~d1);  // AND_Gate
  or or_1 (a, and_1_out, and_2_out, and_3_out, and_4_out);
  or or_2 (b, and_5_out, and_6_out, and_7_out, and_8_out);
  or or_3 (c, and_9_out, and_10_out, and_11_out);
  or or_4 (d, ok_out, ok_2_out, and_12_out, and_13_out, ok_3_out);
  or or_5 (e, and_14_out, and_15_out);
  or or_6 (f, and_16_out, and_17_out, and_18_out, and_19_out);
  or or_7 (g, and_20_out, and_21_out, and_22_out, and_23_out);

  // Notes on the sheet:
  //   B
  //   A
  //   C
  //   D
endmodule
