// Logisim project lab006.circ as structural Verilog: 6 circuits, main circuit soma
// somador
module soma (
  input  a7,
  input  a6,
  input  a5,
  input  a4,
  input  a3,
  input  a2,
  input  a1,
  input  a0,
  input  b7,
  input  b6,
  input  b5,
  input  b4,
  input  b3,
  input  b2,
  input  b1,
  input  b0,
  output S7,
  output S6,
  output S5,
  output S4,
  output S3,
  output S2,
  output S1,
  output S0,
  output out_25
);

  wire N1_r1, N2_r1, N3_r1, N4_r1, N5_r1, N6_r1, somadorn0_1_r0;

  somadorN0 somadorn0_1 (.a0(a0), .b0(b0), .s0(S0), .r0(somadorn0_1_r0));
  somadorNn N1 (.a1(a1), .b1(b1), .r0(somadorn0_1_r0), .s1(S1), .r1(N1_r1));
  somadorNn N2 (.a1(a2), .b1(b2), .r0(N1_r1), .s1(S2), .r1(N2_r1));
  somadorNn N3 (.a1(a3), .b1(b3), .r0(N2_r1), .s1(S3), .r1(N3_r1));
  somadorNn N4 (.a1(a4), .b1(b4), .r0(N3_r1), .s1(S4), .r1(N4_r1));
  somadorNn N5 (.a1(a5), .b1(b5), .r0(N4_r1), .s1(S5), .r1(N5_r1));
  somadorNn N6 (.a1(a6), .b1(b6), .r0(N5_r1), .s1(S6), .r1(N6_r1));
  somadorNn N7 (.a1(a7), .b1(b7), .r0(N6_r1), .s1(S7), .r1(out_25));
endmodule

module somadorN0 (
  input  a0,
  input  b0,
  output s0,
  output r0
);

  xor xor_1 (s0, a0, b0);
  and u_r0 (r0, a0, b0);
endmodule

module somadorNn (
  input  a1,
  input  b1,
  input  r0,
  output s1,
  output r1
);

  wire and_1_out, and_2_out, and_3_out, xor_1_out;

  xor xor_1 (xor_1_out, a1, b1);
  and and_1 (and_1_out, a1, b1);
  and and_2 (and_2_out, r0, a1);
  and and_3 (and_3_out, b1, r0);
  xor xor_2 (s1, xor_1_out, r0);
  or or_1 (r1, and_1_out, and_2_out, and_3_out);
endmodule

module inverteBit (
  input  in_1,
  output out_2
);

  not not_1 (out_2, in_1);
endmodule

module complementoDeDois (
  input  b7,
  input  b6,
  input  b5,
  input  b4,
  input  b3,
  input  b2,
  input  b1,
  input  b0,
  input  c0,
  input  c1,
  input  c2,
  input  c3,
  input  c4,
  input  c5,
  input  c6,
  input  c7,
  output Sinal,
  output S7,
  output S6,
  output S5,
  output S4,
  output S3,
  output S2,
  output S1,
  output S0
);

  wire invertebit_1_out_2, invertebit_2_out_2, invertebit_3_out_2, invertebit_4_out_2, invertebit_5_out_2,
       invertebit_6_out_2, invertebit_7_out_2, invertebit_8_out_2;

  inverteBit invertebit_1 (.in_1(c0), .out_2(invertebit_1_out_2));
  inverteBit invertebit_2 (.in_1(c1), .out_2(invertebit_2_out_2));
  inverteBit invertebit_3 (.in_1(c2), .out_2(invertebit_3_out_2));
  inverteBit invertebit_4 (.in_1(c3), .out_2(invertebit_4_out_2));
  inverteBit invertebit_5 (.in_1(c4), .out_2(invertebit_5_out_2));
  inverteBit invertebit_6 (.in_1(c5), .out_2(invertebit_6_out_2));
  inverteBit invertebit_7 (.in_1(c6), .out_2(invertebit_7_out_2));
  inverteBit invertebit_8 (.in_1(c7), .out_2(invertebit_8_out_2));
  soma soma_1 (
    .a7(invertebit_8_out_2), .a6(invertebit_7_out_2), .a5(invertebit_6_out_2), .a4(invertebit_5_out_2),
    .a3(invertebit_4_out_2), .a2(invertebit_3_out_2), .a1(invertebit_2_out_2), .a0(invertebit_1_out_2),
    .b7(b7), .b6(b6), .b5(b5), .b4(b4), .b3(b3), .b2(b2), .b1(b1), .b0(b0), .S7(S7), .S6(S6), .S5(S5),
    .S4(S4), .S3(S3), .S2(S2), .S1(S1), .S0(S0), .out_25(Sinal));
endmodule

module \subtração  (
  input  b7,
  input  b6,
  input  b5,
  input  b4,
  input  b3,
  input  b2,
  input  b1,
  input  b0,
  input  a7,
  input  a6,
  input  a5,
  input  a4,
  input  a3,
  input  a2,
  input  a1,
  input  a0,
  input  c0,
  input  c1,
  input  c2,
  input  c3,
  input  c4,
  input  c5,
  input  c6,
  input  c7,
  output Sinal,
  output S7,
  output S6,
  output S5,
  output S4,
  output S3,
  output S2,
  output S1,
  output S0
);

  wire complementodedois_1_s0, complementodedois_1_s1, complementodedois_1_s2, complementodedois_1_s3,
       complementodedois_1_s4, complementodedois_1_s5, complementodedois_1_s6, complementodedois_1_s7;

  complementoDeDois complementodedois_1 (
    .c0(a0), .c1(a1), .c2(a2), .c3(a3), .c4(a4), .c5(a5), .c6(a6), .c7(a7), .b7(b7), .b6(b6), .b5(b5),
    .b4(b4), .b3(b3), .b2(b2), .b1(b1), .b0(b0), .S7(complementodedois_1_s7), .S6(complementodedois_1_s6),
    .S5(complementodedois_1_s5), .S4(complementodedois_1_s4), .S3(complementodedois_1_s3),
    .S2(complementodedois_1_s2), .S1(complementodedois_1_s1), .S0(complementodedois_1_s0));  // open: Sinal
  soma soma_1 (
    .a7(c7), .a6(c6), .a5(c5), .a4(c4), .a3(c3), .a2(c2), .a1(c1), .a0(c0), .b7(complementodedois_1_s7),
    .b6(complementodedois_1_s6), .b5(complementodedois_1_s5), .b4(complementodedois_1_s4),
    .b3(complementodedois_1_s3), .b2(complementodedois_1_s2), .b1(complementodedois_1_s1),
    .b0(complementodedois_1_s0), .S7(S7), .S6(S6), .S5(S5), .S4(S4), .S3(S3), .S2(S2), .S1(S1), .S0(S0),
    .out_25(Sinal));
endmodule
