// Logisim project lab07.circ as structural Verilog: 3 circuits, main circuit ex001
module ex001 (
  input  A,
  input  B,
  input  C,
  input  D,
  input  C1,
  input  C0,
  output out_7
);

  wire and_1_out, and_2_out, and_3_out, and_4_out, and_5_out, and_6_out, and_7_out, and_8_out;

  and and_1 (and_1_out, ~C1, ~C0);  // AND_Gate
  and and_2 (and_2_out, ~C1, C0);  // AND_Gate
  and and_3 (and_3_out, C1, ~C0);  // AND_Gate
  and and_4 (and_4_out, C1, C0);
  and and_5 (and_5_out, and_1_out, D);
  and and_6 (and_6_out, and_2_out, C);
  and and_7 (and_7_out, and_3_out, B);
  and and_8 (and_8_out, and_4_out, A);
  or or_1 (out_7, and_5_out, and_6_out, and_7_out, and_8_out);
endmodule

module ex006 (
  input  A,
  input  B,
  input  C,
  input  D,
  output out_5
);

  wire and_1_out, and_2_out, and_3_out, and_4_out;

  and and_1 (and_1_out, ~A, ~C);  // AND_Gate
  and and_2 (and_2_out, ~B, C);  // AND_Gate
  and and_3 (and_3_out, A, C);
  and and_4 (and_4_out, and_1_out, ~D);  // AND_Gate
  or or_1 (out_5, and_4_out, and_2_out, and_3_out);
endmodule

module ex005 (
  input  C1,
  input  C0,
  input  in_3,
  input  in_4,
  input  in_5,
  input  in_6,
  output out_7
);

  Multiplexer #(.select(4)) multiplexer_1 (
    .in0(C1), .in1(C0), .in2(C1), .in3(C1), .in4(C1), .in5(C0), .in6(C0), .in7(C0), .in8(C0), .in9(C0),
    .in10(C1), .in11(C1), .in12(C0), .in13(C0), .in14(C1), .in15(C1), .out(out_7),
    .sel({in_3, in_4, in_5, in_6}));  // open: en
endmodule
