// Logisim project relogio.circ as structural Verilog: 4 circuits, main circuit main
module main (
);

  wire and_1_out, and_2_out, and_3_out, and_4_out, button_1_out, C5_2_q0, C5_2_q1, C5_2_q2, C5_q0, C5_q1,
       C5_q2, C9_2_q1, C9_2_q2, C9_2_q3, C9_2_q4, C9_3_q1, C9_3_q2, C9_3_q3, C9_3_q4, C9_4_q1, C9_4_q2,
       C9_4_q3, C9_4_q4, C9_q1, C9_q2, C9_q3, C9_q4, circdisplay7seg_1_a_2, circdisplay7seg_1_b_2,
       circdisplay7seg_1_c_2, circdisplay7seg_1_d_2, circdisplay7seg_1_e, circdisplay7seg_1_f,
       circdisplay7seg_1_g, circdisplay7seg_1_zero, circdisplay7seg_2_a_2, circdisplay7seg_2_b_2,
       circdisplay7seg_2_c_2, circdisplay7seg_2_d_2, circdisplay7seg_2_e, circdisplay7seg_2_f,
       circdisplay7seg_2_g, circdisplay7seg_2_zero, circdisplay7seg_3_a_2, circdisplay7seg_3_b_2,
       circdisplay7seg_3_c_2, circdisplay7seg_3_d_2, circdisplay7seg_3_e, circdisplay7seg_3_f,
       circdisplay7seg_3_g, circdisplay7seg_3_zero, circdisplay7seg_4_a_2, circdisplay7seg_4_b_2,
       circdisplay7seg_4_c_2, circdisplay7seg_4_d_2, circdisplay7seg_4_e, circdisplay7seg_4_f,
       circdisplay7seg_4_g, circdisplay7seg_4_zero, circdisplay7seg_5_a_2, circdisplay7seg_5_b_2,
       circdisplay7seg_5_c_2, circdisplay7seg_5_d_2, circdisplay7seg_5_e, circdisplay7seg_5_f,
       circdisplay7seg_5_g, circdisplay7seg_5_zero, circdisplay7seg_6_a_2, circdisplay7seg_6_b_2,
       circdisplay7seg_6_c_2, circdisplay7seg_6_d_2, circdisplay7seg_6_e, circdisplay7seg_6_f,
       circdisplay7seg_6_g, circdisplay7seg_6_zero, clock_out, t_ff_1_q;

  Button button_1 (.out(button_1_out));
  and and_1 (and_1_out, and_2_out, and_3_out);
  T_Flip_Flop t_ff_1 (.clk(button_1_out), .T(1'b1), .Q(t_ff_1_q));  // open: Qn, preset, reset, en
  and and_2 (and_2_out, ~C9_2_q1, ~C9_2_q2, C9_2_q3);  // AND_Gate
  and and_3 (and_3_out, ~C9_q1, C9_q2);  // AND_Gate
  Clock clock (.out(clock_out));
  circDisplay7Seg circdisplay7seg_1 (
    .a_2(circdisplay7seg_1_a_2), .b_2(circdisplay7seg_1_b_2), .c_2(circdisplay7seg_1_c_2),
    .d_2(circdisplay7seg_1_d_2), .e(circdisplay7seg_1_e), .f(circdisplay7seg_1_f), .g(circdisplay7seg_1_g),
    .A(C9_q1), .B(C9_q2), .C(C9_q3), .D(C9_q4), .zero(circdisplay7seg_1_zero));
  _7_Segment_Display u_7_segment_display_1 (
    .g(circdisplay7seg_1_g), .f(circdisplay7seg_1_f), .a(circdisplay7seg_1_a_2), .b(circdisplay7seg_1_b_2),
    .e(circdisplay7seg_1_e), .d(circdisplay7seg_1_d_2), .c(circdisplay7seg_1_c_2), .dp(circdisplay7seg_1_zero));
  cont9 C9 (.Tick(C9_2_q4), .Limpar(and_1_out), .q1(C9_q1), .q2(C9_q2), .q3(C9_q3), .q4(C9_q4));
  and and_4 (and_4_out, t_ff_1_q, clock_out);
  circDisplay7Seg circdisplay7seg_2 (
    .a_2(circdisplay7seg_2_a_2), .b_2(circdisplay7seg_2_b_2), .c_2(circdisplay7seg_2_c_2),
    .d_2(circdisplay7seg_2_d_2), .e(circdisplay7seg_2_e), .f(circdisplay7seg_2_f), .g(circdisplay7seg_2_g),
    .A(C9_2_q1), .B(C9_2_q2), .C(C9_2_q3), .D(C9_2_q4), .zero(circdisplay7seg_2_zero));
  _7_Segment_Display u_7_segment_display_2 (
    .g(circdisplay7seg_2_g), .f(circdisplay7seg_2_f), .a(circdisplay7seg_2_a_2), .b(circdisplay7seg_2_b_2),
    .e(circdisplay7seg_2_e), .d(circdisplay7seg_2_d_2), .c(circdisplay7seg_2_c_2), .dp(circdisplay7seg_2_zero));
  cont9 C9_2 (.Tick(C5_q2), .Limpar(and_1_out), .q1(C9_2_q1), .q2(C9_2_q2), .q3(C9_2_q3), .q4(C9_2_q4));
  circDisplay7Seg circdisplay7seg_3 (
    .a_2(circdisplay7seg_3_a_2), .b_2(circdisplay7seg_3_b_2), .c_2(circdisplay7seg_3_c_2),
    .d_2(circdisplay7seg_3_d_2), .e(circdisplay7seg_3_e), .f(circdisplay7seg_3_f), .g(circdisplay7seg_3_g),
    .A(C5_q0), .B(C5_q1), .C(C5_q2), .D(1'b0), .zero(circdisplay7seg_3_zero));
  _7_Segment_Display u_7_segment_display_3 (
    .g(circdisplay7seg_3_g), .f(circdisplay7seg_3_f), .a(circdisplay7seg_3_a_2), .b(circdisplay7seg_3_b_2),
    .e(circdisplay7seg_3_e), .d(circdisplay7seg_3_d_2), .c(circdisplay7seg_3_c_2), .dp(circdisplay7seg_3_zero));
  cont5 C5 (.Tick(C9_3_q4), .q0(C5_q0), .q1(C5_q1), .q2(C5_q2));
  circDisplay7Seg circdisplay7seg_4 (
    .a_2(circdisplay7seg_4_a_2), .b_2(circdisplay7seg_4_b_2), .c_2(circdisplay7seg_4_c_2),
    .d_2(circdisplay7seg_4_d_2), .e(circdisplay7seg_4_e), .f(circdisplay7seg_4_f), .g(circdisplay7seg_4_g),
    .A(C9_3_q1), .B(C9_3_q2), .C(C9_3_q3), .D(C9_3_q4), .zero(circdisplay7seg_4_zero));
  _7_Segment_Display u_7_segment_display_4 (
    .g(circdisplay7seg_4_g), .f(circdisplay7seg_4_f), .a(circdisplay7seg_4_a_2), .b(circdisplay7seg_4_b_2),
    .e(circdisplay7seg_4_e), .d(circdisplay7seg_4_d_2), .c(circdisplay7seg_4_c_2), .dp(circdisplay7seg_4_zero));
  cont9 C9_3 (.Tick(C5_2_q2), .q1(C9_3_q1), .q2(C9_3_q2), .q3(C9_3_q3), .q4(C9_3_q4));  // open: Limpar
  circDisplay7Seg circdisplay7seg_5 (
    .a_2(circdisplay7seg_5_a_2), .b_2(circdisplay7seg_5_b_2), .c_2(circdisplay7seg_5_c_2),
    .d_2(circdisplay7seg_5_d_2), .e(circdisplay7seg_5_e), .f(circdisplay7seg_5_f), .g(circdisplay7seg_5_g),
    .A(C5_2_q0), .B(C5_2_q1), .C(C5_2_q2), .D(1'b0), .zero(circdisplay7seg_5_zero));
  circDisplay7Seg circdisplay7seg_6 (
    .a_2(circdisplay7seg_6_a_2), .b_2(circdisplay7seg_6_b_2), .c_2(circdisplay7seg_6_c_2),
    .d_2(circdisplay7seg_6_d_2), .e(circdisplay7seg_6_e), .f(circdisplay7seg_6_f), .g(circdisplay7seg_6_g),
    .A(C9_4_q1), .B(C9_4_q2), .C(C9_4_q3), .D(C9_4_q4), .zero(circdisplay7seg_6_zero));
  _7_Segment_Display u_7_segment_display_5 (
    .g(circdisplay7seg_5_g), .f(circdisplay7seg_5_f), .a(circdisplay7seg_5_a_2), .b(circdisplay7seg_5_b_2),
    .e(circdisplay7seg_5_e), .d(circdisplay7seg_5_d_2), .c(circdisplay7seg_5_c_2), .dp(circdisplay7seg_5_zero));
  cont5 C5_2 (.Tick(C9_4_q4), .q0(C5_2_q0), .q1(C5_2_q1), .q2(C5_2_q2));
  _7_Segment_Display u_7_segment_display_6 (
    .g(circdisplay7seg_6_g), .f(circdisplay7seg_6_f), .a(circdisplay7seg_6_a_2), .b(circdisplay7seg_6_b_2),
    .e(circdisplay7seg_6_e), .d(circdisplay7seg_6_d_2), .c(circdisplay7seg_6_c_2), .dp(circdisplay7seg_6_zero));
  cont9 C9_4 (.Tick(and_4_out), .q1(C9_4_q1), .q2(C9_4_q2), .q3(C9_4_q3), .q4(C9_4_q4));  // open: Limpar
endmodule

module circDisplay7Seg (
  input  A,
  input  B,
  input  C,
  input  D,
  output a_2,
  output b_2,
  output c_2,
  output d_2,
  output e,
  output f,
  output g,
  output zero
);

  Multiplexer #(.select(4)) multiplexer_1 (
    .in0(1'b1), .in1(1'b0), .in2(1'b1), .in3(1'b1), .in4(1'b0), .in5(1'b1), .in6(1'b1), .in7(1'b1),
    .in8(1'b1), .in9(1'b1), .in10(1'b0), .in11(1'b0), .in12(1'b0), .in13(1'b0), .in14(1'b0), .in15(1'b0),
    .out(a_2), .sel({D, C, B, A}));  // open: en
  Multiplexer #(.select(4)) multiplexer_2 (
    .in0(1'b1), .in1(1'b1), .in2(1'b1), .in3(1'b1), .in4(1'b1), .in5(1'b0), .in6(1'b0), .in7(1'b1),
    .in8(1'b1), .in9(1'b1), .in10(1'b0), .in11(1'b0), .in12(1'b0), .in13(1'b0), .in14(1'b0), .in15(1'b0),
    .out(b_2), .sel({D, C, B, A}));  // open: en
  Multiplexer #(.select(4)) multiplexer_3 (
    .in0(1'b1), .in1(1'b1), .in2(1'b0), .in3(1'b1), .in4(1'b1), .in5(1'b1), .in6(1'b1), .in7(1'b1),
    .in8(1'b1), .in9(1'b1), .in10(1'b0), .in11(1'b0), .in12(1'b0), .in13(1'b0), .in14(1'b0), .in15(1'b0),
    .out(c_2), .sel({D, C, B, A}));  // open: en
  Multiplexer #(.select(4)) multiplexer_4 (
    .in0(1'b1), .in1(1'b0), .in2(1'b1), .in3(1'b1), .in4(1'b0), .in5(1'b1), .in6(1'b1), .in7(1'b0),
    .in8(1'b1), .in9(1'b1), .in10(1'b0), .in11(1'b0), .in12(1'b0), .in13(1'b0), .in14(1'b0), .in15(1'b0),
    .out(d_2), .sel({D, C, B, A}));  // open: en
  Multiplexer #(.select(4)) multiplexer_5 (
    .in0(1'b1), .in1(1'b0), .in2(1'b1), .in3(1'b0), .in4(1'b0), .in5(1'b0), .in6(1'b1), .in7(1'b0),
    .in8(1'b1), .in9(1'b0), .in10(1'b0), .in11(1'b0), .in12(1'b0), .in13(1'b0), .in14(1'b0), .in15(1'b0),
    .out(e), .sel({D, C, B, A}));  // open: en
  Multiplexer #(.select(4)) multiplexer_6 (
    .in0(1'b1), .in1(1'b0), .in2(1'b0), .in3(1'b0), .in4(1'b1), .in5(1'b1), .in6(1'b1), .in7(1'b0),
    .in8(1'b1), .in9(1'b1), .in10(1'b0), .in11(1'b0), .in12(1'b0), .in13(1'b0), .in14(1'b0), .in15(1'b0),
    .out(f), .sel({D, C, B, A}));  // open: en
  Multiplexer #(.select(4)) multiplexer_7 (
    .in0(1'b0), .in1(1'b0), .in2(1'b1), .in3(1'b1), .in4(1'b1), .in5(1'b1), .in6(1'b1), .in7(1'b0),
    .in8(1'b1), .in9(1'b1), .in10(1'b0), .in11(1'b0), .in12(1'b0), .in13(1'b0), .in14(1'b0), .in15(1'b0),
    .out(g), .sel({D, C, B, A}));  // open: en

  assign zero = 1'b0;
endmodule

module cont9 (
  input  Tick,
  input  Limpar,
  output q1,
  output q2,
  output q3,
  output q4
);

  wire and_1_out, or_1_out;

  or or_1 (or_1_out, Limpar, and_1_out);
  T_Flip_Flop #(.trigger("falling")) t_ff_1 (.clk(Tick), .T(1'b1), .Q(q1), .reset(or_1_out));  // open: Qn, preset, en
  T_Flip_Flop #(.trigger("falling")) t_ff_2 (.clk(q1), .T(1'b1), .Q(q2), .reset(or_1_out));  // open: Qn, preset, en
  and and_1 (and_1_out, ~q1, q2, ~q3, q4);  // AND_Gate
  T_Flip_Flop #(.trigger("falling")) t_ff_3 (.clk(q2), .T(1'b1), .Q(q3), .reset(or_1_out));  // open: Qn, preset, en
  T_Flip_Flop #(.trigger("falling")) t_ff_4 (.clk(q3), .T(1'b1), .Q(q4), .reset(or_1_out));  // open: Qn, preset, en
endmodule

module cont5 (
  input  Tick,
  output q0,
  output q1,
  output q2
);

  wire and_1_out;

  T_Flip_Flop #(.trigger("falling")) t_ff_1 (.clk(Tick), .T(1'b1), .Q(q0), .reset(and_1_out));  // open: Qn, preset, en
  T_Flip_Flop #(.trigger("falling")) t_ff_2 (.clk(q0), .T(1'b1), .Q(q1), .reset(and_1_out));  // open: Qn, preset, en
  and and_1 (and_1_out, ~q0, q1, q2);  // AND_Gate
  T_Flip_Flop #(.trigger("falling")) t_ff_3 (.clk(q1), .T(1'b1), .Q(q2), .reset(and_1_out));  // open: Qn, preset, en
endmodule
